# Fritzing sketch Behavioral Box Circuit (saved by Fritzing 0.9.10b)
circuit board: 17.1557cm x 10.4674cm
breadboards: 2

parts:
  Q1 = TIP120 Hi-Current Darlington Transistor
  A1 = Teensy 4.1
  Part1 = Audio FX Sound Board + 2x2W Amp
  U1 = JOYSTICK-PSP1000 [package=joystick-psp1000]
  SP1 = SPEAKER [package=pcb_mount_speaker]
  R1 = Resistor [tolerance=±5% power=0.25 resistance=1000 package=THT]
  D1 = Rectifier Diode [part_number=1N4001 package="300 mil [THT]"]
  Q2 = TRANSISTOR_NPN [package=to-92-ammo]
  R2 = Resistor [tolerance=±1% power=0.25 resistance=1000 package=THT]
  D2 = Rectifier Diode [part_number=1N4001 package="300 mil [THT]"]
  L2 = Solenoid
  L1 = Solenoid

nets:
  N1: Q1.BASE, R1.Pin_1
  N2: Q1.COLLECTOR, D1.anode
  GND: Q1.EMITTER, A1.Pin_12, A1.Pin_38, A1.Pin_50, A1.Pin_63, Part1.GND, Part1.UG, U1.GND, Q2.C
  N3: A1.Pin_13, Part1.TX
  N4: A1.Pin_14, Part1.RX
  N5: A1.Pin_17, R2.Pin_0
  N6: A1.Pin_23, R1.Pin_0
  N7: A1.Pin_26, A1.Pin_62, U1.VCC
  N8: A1.Pin_52, U1.X
  N9: A1.Pin_53, U1.Y
  N10: A1.Pin_57, Part1.RST
  N11: A1.Pin_64, D1.cathode, D2.cathode, L2.pin2, L1.pin2
  N12: Part1.R+, SP1.-
  N13: Part1.R-, SP1.+
  N14: Q2.E, D2.anode, L2.pin1
  N15: Q2.B, R2.Pin_1

notes:
  Air Puff Solenoid
  Water Delivery Solenoid

custom parts:
  Teensy 4.1: The Teensy is a complete USB-based microcontoller development system, in a very small footprint, capable of implementing many types of projects. All programming is done via the USB port. No special programmer is needed, only a standard micro-USB cable and a PC or Macintosh with a USB port.
  Audio FX Sound Board + 2x2W Amp: The Adafruit Sound Board, the fastest way to add audio effects to a project!
